// Logisim project Project1.circ as structural Verilog: 4 circuits, main circuit main
module main (
);

  wire Clock_out, Decode_we, Execute_we_2, Memory_we_2, registerfile_1_p2, WE_2_q, WE_q;
  wire [2:0] Control_q, Decode_control;
  wire [3:0] Decode_op_2, Op_2_q;
  wire [4:0] Decode_rd, Decode_sa, Execute_rd_2, Memory_rd_2, ra_q, rb_q, rd_2_q, rd_q, registerfile_1_p3,
       Sa_q;
  wire [31:0] A_q, B_q, C_q, Decode_i, Execute_c, Execute_pc_2, I_q, Memory_c_2, Memory_pc_2,
       mipsprogramrom_1_p1, mipsprogramrom_1_p2, Op_q, PC_2_q, PC_3_q, PC_q, registerfile_1_p1,
       registerfile_1_p6, registerfile_1_p7;

  Clock Clock (.out(Clock_out));
  // MIPSProgramROM mipsprogramrom_1: pin names not known; wires that end beside it: mipsprogramrom_1_p1, mipsprogramrom_1_p2
  Register #(.width(32)) Op (.D(mipsprogramrom_1_p2), .Q(Op_q), .clk(Clock_out));  // open: en, clr
  Register #(.width(32)) PC (.D(mipsprogramrom_1_p1), .Q(PC_q), .clk(Clock_out));  // open: en, clr
  // RegisterFile registerfile_1: pin names not known; wires that end beside it: registerfile_1_p1, registerfile_1_p2, registerfile_1_p3, Op_q[25:21], Op_q[20:16], registerfile_1_p6, registerfile_1_p7
  Decode Decode (
    .Immediate_Function_Sa(Op_q[15:0]), .Op(Op_q[31:26]), .I(Decode_i), .Sa(Decode_sa), .Op_2(Decode_op_2),
    .Control(Decode_control), .Rd(Decode_rd), .WE(Decode_we));
  Register #(.width(32)) A (.D(registerfile_1_p6), .Q(A_q), .clk(Clock_out));  // open: en, clr
  Register #(.width(5)) ra (.D(Op_q[25:21]), .Q(ra_q), .clk(Clock_out));  // open: en, clr
  Register #(.width(32)) B (.D(registerfile_1_p7), .Q(B_q), .clk(Clock_out));  // open: en, clr
  Register #(.width(5)) rb (.D(Op_q[20:16]), .Q(rb_q), .clk(Clock_out));  // open: en, clr
  Register #(.width(32)) I (.D(Decode_i), .Q(I_q), .clk(Clock_out));  // open: en, clr
  Register #(.width(5)) Sa (.D(Decode_sa), .Q(Sa_q), .clk(Clock_out));  // open: en, clr
  Register #(.width(4)) Op_2 (.D(Decode_op_2), .Q(Op_2_q), .clk(Clock_out));  // open: en, clr
  Register #(.width(3)) Control (.D(Decode_control), .Q(Control_q), .clk(Clock_out));  // open: en, clr
  Register #(.width(5)) rd (.D(Decode_rd), .Q(rd_q), .clk(Clock_out));  // open: en, clr
  Register #(.width(32)) PC_2 (.D(PC_q), .Q(PC_2_q), .clk(Clock_out));  // open: en, clr
  Register #(.width(1)) WE (.D(Decode_we), .Q(WE_q), .clk(Clock_out));  // open: en, clr
  Execute Execute (
    .A(A_q), .Ra(ra_q), .B(B_q), .Rb(rb_q), .I(I_q), .Sa(Sa_q), .Op(Op_2_q), .Control(Control_q), .rd(rd_q),
    .PC(PC_2_q), .WE(WE_q), .C(Execute_c), .rd_2(Execute_rd_2), .PC_2(Execute_pc_2), .WE_2(Execute_we_2));
  Register #(.width(32)) C (.D(Execute_c), .Q(C_q), .clk(Clock_out));  // open: en, clr
  Register #(.width(5)) rd_2 (.D(Execute_rd_2), .Q(rd_2_q), .clk(Clock_out));  // open: en, clr
  Register #(.width(32)) PC_3 (.D(Execute_pc_2), .Q(PC_3_q), .clk(Clock_out));  // open: en, clr
  Register #(.width(1)) WE_2 (.D(Execute_we_2), .Q(WE_2_q), .clk(Clock_out));  // open: en, clr
  Memory Memory (
    .C(C_q), .rd(rd_2_q), .PC(PC_3_q), .WE(WE_2_q), .C_2(Memory_c_2), .rd_2(Memory_rd_2), .PC_2(Memory_pc_2),
    .WE_2(Memory_we_2));
  Register #(.width(32)) C_2 (.D(Memory_c_2), .Q(registerfile_1_p1), .clk(Clock_out));  // open: en, clr
  Register #(.width(5)) rd_3 (.D(Memory_rd_2), .Q(registerfile_1_p3), .clk(Clock_out));  // open: en, clr
  Register #(.width(32)) PC_4 (.D(Memory_pc_2), .Q(mipsprogramrom_1_p1), .clk(Clock_out));  // open: en, clr
  Register #(.width(1)) WE_3 (.D(Memory_we_2), .Q(registerfile_1_p2), .clk(Clock_out));  // open: en, clr

  // Notes on the sheet:
  //   Stage: Fetch
  //   Stage: Decode
  //   Stage: Writeback
  //   Stage: Execute
  //   Stage: Memory
  //   Stage: Writeback
endmodule

module Memory (
  input  [31:0] C,
  input  [4:0] rd,
  input  [31:0] PC,
  input  WE,
  output [31:0] C_2,
  output [4:0] rd_2,
  output [31:0] PC_2,
  output WE_2
);


  assign C_2 = C;
  assign PC_2 = PC;
  assign rd_2 = rd;
  assign WE_2 = WE;
endmodule

module Execute (
  input  [31:0] A,
  input  [4:0] Ra,
  input  [31:0] B,
  input  [4:0] Rb,
  input  [31:0] I,
  input  [4:0] Sa,
  input  [3:0] Op,
  input  [2:0] Control,
  input  [4:0] rd,
  input  [31:0] PC,
  input  WE,
  output [31:0] C,
  output [4:0] rd_2,
  output [31:0] PC_2,
  output WE_2
);

  wire comparator_1_lt, comparator_2_lt, multiplexer_4_out, not_1_out;
  wire [4:0] mips_alu_1_p4;
  wire [31:0] bit_extender_1_out, mips_alu_1_p5, multiplexer_1_out;

  Multiplexer #(.width(32), .enable("false")) multiplexer_1 (
    .in0(B), .in1(I), .out(multiplexer_1_out), .sel(Control[2]));
  // Mips_ALU mips_alu_1: pin names not known; wires that end beside it: A, multiplexer_1_out, Op, mips_alu_1_p4, mips_alu_1_p5
  Multiplexer #(.width(5), .enable("false")) multiplexer_2 (
    .in0(A[4:0]), .in1(Sa), .out(mips_alu_1_p4), .sel(Control[0]));
  Multiplexer #(.width(5), .enable("false")) multiplexer_3 (.in0(Rb), .in1(rd), .out(rd_2), .sel(Control[2]));
  Comparator #(.width(32)) comparator_1 (.a(A), .b(multiplexer_1_out), .lt(comparator_1_lt));  // open: gt, eq
  Comparator #(.width(32), .mode("unsigned")) comparator_2 (
    .a(A), .b(multiplexer_1_out), .lt(comparator_2_lt));  // open: gt, eq
  Multiplexer #(.enable("false")) multiplexer_4 (
    .in0(comparator_1_lt), .in1(comparator_2_lt), .out(multiplexer_4_out), .sel(Control[0]));
  assign bit_extender_1_out = {{31{1'b0}}, multiplexer_4_out};  // Bit_Extender bit_extender_1
  Multiplexer #(.width(32), .enable("false")) multiplexer_5 (
    .in0(bit_extender_1_out), .in1(mips_alu_1_p5), .out(C), .sel(not_1_out));
  not not_1 (not_1_out, Control[1]);

  assign PC_2 = PC;
  assign WE_2 = WE;

  // Notes on the sheet:
  //   If it is an immediate operation, the destination register is stored in the bits 22-17
endmodule

module Decode (
  input  [15:0] Immediate_Function_Sa,
  input  [5:0] Op,
  output [31:0] I,
  output [4:0] Sa,
  output [3:0] Op_2,
  output [2:0] Control,
  output [4:0] Rd,
  output WE
);

  wire [31:0] bit_extender_1_out;

  assign bit_extender_1_out = {{16{Immediate_Function_Sa[15]}}, Immediate_Function_Sa};  // Bit_Extender bit_extender_1
  Multiplexer #(.width(32), .enable("false")) multiplexer_1 (
    .in0(bit_extender_1_out), .in1({Immediate_Function_Sa, {16{1'b0}}}), .out(I));  // open: sel

  assign Rd = Immediate_Function_Sa[15:11];
  assign Sa = Immediate_Function_Sa[10:6];
endmodule
